# Fritzing sketch Nixie_clock_pcb3 (saved by Fritzing 0.9.3b)
circuit board: 20.6189cm x 11.9124cm
breadboards: 1

parts:
  R3 = Resistor [tolerance=±5% resistance=220 package=THT]
  R4 = Resistor [tolerance=±5% resistance=220 package=THT]
  C1 = Electrolytic Capacitor [capacitance=1µF package="100 mil [THT, electrolytic]"]
  C2 = Electrolytic Capacitor [capacitance=1µF package="100 mil [THT, electrolytic]"]
  IC4 = ULN2003A [package="DIP16 [THT]"]
  XTAL1 = Crystal [frequency="16 Mhz" package=THT]
  C3 = Ceramic Capacitor [capacitance=100nF package="100 mil [THT, multilayer]"]
  C4 = Ceramic Capacitor [capacitance=100nF package="100 mil [THT, multilayer]"]
  T2 = LM35 Temperature Sensor [package="TO92 [THT]"]
  T5 = LM35 Temperature Sensor [package="TO92 [THT]"]
  T6 = LM35 Temperature Sensor [package="TO92 [THT]"]
  C9 = Ceramic Capacitor [capacitance=100nF package="200 mil [THT, multilayer]"]
  C11 = Ceramic Capacitor [capacitance=100nF package="200 mil [THT, multilayer]"]
  R6 = Resistor [tolerance=±5% resistance=220 package=THT]
  C16 = Film/Foil Capacitor [capacitance=100nF voltage=35V package="15mm [THT, pp]"]
  R10 = Resistor [tolerance=±5% resistance=220 package=THT]
  R11 = Resistor [tolerance=±5% resistance=220 package=THT]
  IC8 = ULN2003A [package="DIP16 [THT]"]
  T8 = LM35 Temperature Sensor [package="TO92 [THT]"]
  T11 = LM35 Temperature Sensor [package="TO92 [THT]"]
  T12 = LM35 Temperature Sensor [package="TO92 [THT]"]
  C21 = Ceramic Capacitor [capacitance=100nF package="200 mil [THT, multilayer]"]
  C26 = Ceramic Capacitor [capacitance=100nF package="200 mil [THT, multilayer]"]
  R13 = Resistor [tolerance=±5% resistance=220 package=THT]
  C31 = Film/Foil Capacitor [capacitance=100nF voltage=35V package="15mm [THT, pp]"]
  180V = Header 2 [package=screwterminal-3.5mm-2_lock]
  LED = LED - 5mm [color="Red (633nm)" package="5 mm [THT]"]
  LED2 = LED - 5mm [color="Red (633nm)" package="5 mm [THT]"]
  R14 = Resistor [tolerance=±5% resistance=220 package=THT]
  R15 = Resistor [tolerance=±5% resistance=220 package=THT]
  R17 = Resistor [tolerance=±5% resistance=220 package=THT]
  R18 = Resistor [tolerance=±5% resistance=220 package=THT]
  R19 = Resistor [tolerance=±5% resistance=220 package=THT]
  R20 = Resistor [tolerance=±5% resistance=220 package=THT]
  R21 = Resistor [tolerance=±5% resistance=220 package=THT]
  R22 = Resistor [tolerance=±5% resistance=220 package=THT]
  IC9 = ULN2003A [package="DIP16 [THT]"]
  IC10 = ULN2003A [package="DIP16 [THT]"]
  T13 = LM35 Temperature Sensor [package="TO92 [THT]"]
  T14 = LM35 Temperature Sensor [package="TO92 [THT]"]
  T15 = LM35 Temperature Sensor [package="TO92 [THT]"]
  T16 = LM35 Temperature Sensor [package="TO92 [THT]"]
  T17 = LM35 Temperature Sensor [package="TO92 [THT]"]
  T18 = LM35 Temperature Sensor [package="TO92 [THT]"]
  C32 = Ceramic Capacitor [capacitance=100nF package="200 mil [THT, multilayer]"]
  C33 = Ceramic Capacitor [capacitance=100nF package="200 mil [THT, multilayer]"]
  C34 = Ceramic Capacitor [capacitance=100nF package="200 mil [THT, multilayer]"]
  C35 = Ceramic Capacitor [capacitance=100nF package="200 mil [THT, multilayer]"]
  R23 = Resistor [tolerance=±5% resistance=220 package=THT]
  R24 = Resistor [tolerance=±5% resistance=220 package=THT]
  C36 = Film/Foil Capacitor [capacitance=100nF voltage=35V package="15mm [THT, pp]"]
  C37 = Film/Foil Capacitor [capacitance=100nF voltage=35V package="15mm [THT, pp]"]
  LED3 = LED - 5mm [color="Red (633nm)" package="5 mm [THT]"]
  LED4 = LED - 5mm [color="Red (633nm)" package="5 mm [THT]"]
  C38 = Ceramic Capacitor [capacitance=100nF package="200 mil [THT, multilayer]"]
  R25 = Resistor [tolerance=±5% resistance=220 package=THT]
  12V = Header 2 [package=screwterminal-3.5mm-2_lock]
  U1 = atmega328 [package=dip]
  U2 = Voltage Regulator - 5V [package="TO220 [THT]"]
  R26 = Resistor [tolerance=±5% resistance=220 package=THT]
  R27 = Resistor [tolerance=±5% resistance=220 package=THT]
  R28 = Resistor [tolerance=±5% resistance=220 package=THT]
  R29 = Resistor [tolerance=±5% resistance=220 package=THT]
  R30 = Resistor [tolerance=±5% resistance=220 package=THT]
  C39 = Ceramic Capacitor [capacitance=100nF package="200 mil [THT, multilayer]"]
  C40 = Ceramic Capacitor [capacitance=100nF package="200 mil [THT, multilayer]"]
  C41 = Ceramic Capacitor [capacitance=100nF package="200 mil [THT, multilayer]"]
  C42 = Ceramic Capacitor [capacitance=100nF package="200 mil [THT, multilayer]"]
  C43 = Ceramic Capacitor [capacitance=100nF package="200 mil [THT, multilayer]"]
  R32 = Resistor [tolerance=±5% resistance=220 package=THT]
  C45 = Film/Foil Capacitor [capacitance=100nF voltage=35V package="15mm [THT, pp]"]
  ANT1 = Antenna  # not connected
  ANT2 = Antenna  # not connected
  ANT3 = Antenna  # not connected
  ANT4 = Antenna  # not connected
  J1 = female pin header, 2 pins [form="♀ (female)"]
  J2 = female pin header, 2 pins [form="♀ (female)"]

nets:
  N1: R3.Pin_0, R6.Pin_1
  N2: R3.Pin_1, R10.Pin_1, 180V.1, R17.Pin_1, R18.Pin_1, R25.Pin_0
  N3: R4.Pin_0, C3.0, C4.0, U1.GND#7, C45.-
  N4: R4.Pin_1, IC4.In_5
  N5: C1.-, C2.-, R11.Pin_0, 180V.2, 12V.1, U2.GND, C39.1, C40.1, C41.1, C42.1, C43.1, C45.+
  N6: C1.+, 12V.2, U2.input_voltage
  N7: C2.+, R14.Pin_1, R15.Pin_1, R20.Pin_1, R22.Pin_1, U1.VCC, U2.output_voltage, R27.Pin_0, R28.Pin_0, R29.Pin_0, R30.Pin_1, R32.Pin_1, J2.pin2
  N8: IC4.In_1, T6.GND
  N9: IC4.In_2, R6.Pin_0
  N10: IC4.In_3, C11.1
  N11: IC4.In_4, T5.GND
  N12: IC4.In_6, T2.Vout
  N13: IC4.In_7, T2.GND
  N14: IC4.0V, C9.0
  N15: IC4.COM_-_Common, C16.+
  N16: IC4.Out_7, U1.D5_(PWM)
  N17: IC4.Out_6, U1.D6_(PWM)
  N18: IC4.Out_5, R27.Pin_1
  N19: IC4.Out_4, U1.D7
  N20: IC4.Out_3, U1.D8
  N21: IC4.Out_2, T6.Vout
  N22: IC4.Out_1, T6.+Vs
  N23: XTAL1.pin_0, C4.1, U1.XLAT1
  N24: XTAL1.pin_1, C3.1, U1.XLAT2
  N25: T2.+Vs, C11.0
  N26: T5.+Vs, C16.-
  N27: T5.Vout, C9.1
  N28: R10.Pin_0, R13.Pin_1
  N29: R11.Pin_1, IC8.In_5
  N30: IC8.In_1, T12.GND
  N31: IC8.In_2, R13.Pin_0
  N32: IC8.In_3, C21.1
  N33: IC8.In_4, T11.GND
  N34: IC8.In_6, T8.Vout
  N35: IC8.In_7, T8.GND
  N36: IC8.0V, C26.0
  N37: IC8.COM_-_Common, C31.+
  N38: IC8.Out_7, U1.D1_(TX)
  N39: IC8.Out_6, U1.D2
  N40: IC8.Out_5, R28.Pin_1
  N41: IC8.Out_4, U1.D3_(PWM)
  N42: IC8.Out_3, U1.D4
  N43: IC8.Out_2, T12.Vout
  N44: IC8.Out_1, T12.+Vs
  N45: T8.+Vs, C21.0
  N46: T11.+Vs, C31.-
  N47: T11.Vout, C26.1
  N48: LED.cathode, C39.0
  N49: LED.anode, R14.Pin_0
  N50: LED2.cathode, C40.0
  N51: LED2.anode, R15.Pin_0
  N52: R17.Pin_0, R23.Pin_1
  N53: R18.Pin_0, R24.Pin_1
  N54: R19.Pin_0, R21.Pin_0, C38.1, U1.GND#21, C43.0, J2.pin1
  N55: R19.Pin_1, IC9.In_5
  N56: R20.Pin_0, LED3.anode
  N57: R21.Pin_1, IC10.In_5
  N58: R22.Pin_0, LED4.anode
  N59: IC9.In_1, T18.GND
  N60: IC9.In_2, R23.Pin_0
  N61: IC9.In_3, C34.1
  N62: IC9.In_4, T16.GND
  N63: IC9.In_6, T13.Vout
  N64: IC9.In_7, T13.GND
  N65: IC9.0V, C32.0
  N66: IC9.COM_-_Common, C36.+
  N67: IC9.Out_7, U1.A0
  N68: IC9.Out_6, U1.A1
  N69: IC9.Out_5, R29.Pin_1
  N70: IC9.Out_4, U1.A2
  N71: IC9.Out_3, U1.A3
  N72: IC9.Out_2, T18.Vout
  N73: IC9.Out_1, T18.+Vs
  N74: IC10.In_1, T17.GND
  N75: IC10.In_2, R24.Pin_0
  N76: IC10.In_3, C33.1
  N77: IC10.In_4, T15.GND
  N78: IC10.In_6, T14.Vout
  N79: IC10.In_7, T14.GND
  N80: IC10.0V, C35.0
  N81: IC10.COM_-_Common, C37.+
  N82: IC10.Out_7, U1.D9_(PWM)
  N83: IC10.Out_6, U1.D10_(PWM)
  N84: IC10.Out_5, R26.Pin_1
  N85: IC10.Out_4, U1.D11_(PWM)
  N86: IC10.Out_3, U1.D12
  N87: IC10.Out_2, T17.Vout
  N88: IC10.Out_1, T17.+Vs
  N89: T13.+Vs, C34.0
  N90: T14.+Vs, C33.0
  N91: T15.+Vs, C37.-
  N92: T15.Vout, C35.1
  N93: T16.+Vs, C36.-
  N94: T16.Vout, C32.1
  N95: LED3.cathode, C41.0
  N96: LED4.cathode, C42.0
  N97: C38.0, R25.Pin_1
  N98: U1.RESET, R30.Pin_0
  N99: U1.AVCC, U1.AREF, R26.Pin_0, R32.Pin_0
  N100: U1.A4, J1.pin2
  N101: U1.A5, J1.pin1
